// Logisim project MIPS32.circ as structural Verilog: 1 circuit, main circuit main
module main (
);

  Register register_1 ();  // open: D, en, Q, clk, clr
  // Incrementer incrementer_1: pin names not known
  // MIPSProgramROM mipsprogramrom_1: pin names not known
  // RegisterFile registerfile_1: pin names not known
endmodule
